# Fritzing sketch CircuitQ (saved by Fritzing 0.9.4)
breadboards: 1

parts:
  D1 = Schottky Diode [part_number=1N5817 package="Melf DO-213 AB [SMD]"]
  R1 = Resistor [tolerance=±5% resistance=330 package="1206 [SMD]"]
  IC1 = Hex Inverter Schmitt Trigger SN74HC14 [package="DIP (Dual Inline)"]
  Part1 = Arduino Mega 2560 (Rev3)
  J1 = shrouded pin header, 6 pins [form="♂ (shrouded male)"]  # not connected
  U1 = Sharp PC817 [part_number=PC817XI package=SMT]
  M1 = DOIT Esp32 DevKit v1 (30 pins long, 11 pins width) [part_number=ESP32S-PIN30]

nets:
  VCC: D1.cathode, IC1.VCC, Part1.5V, U1.Pin_1
  N1: D1.anode, R1.Pin_0, U1.Pin_2
  N2: R1.Pin_1, IC1.3Y
  N3: IC1.1Y, Part1.D19/RX1
  N4: IC1.2A, Part1.D18/TX1
  GND: IC1.GND, Part1.GND, U1.Pin_3, M1.GND
  N5: Part1.D17_PWM/RX2, M1.TX0
  N6: Part1.D16_PWM/TX2, M1.RX0

notes:
  MDB Connector
  RX, TX, CommGnd
  0 , GND, 0
  Wire A and B
  Short them to start comm
  74HC04N Hex Inverter
  PC817 Optocoupler
  1N4007 Diode

custom parts:
  DOIT Esp32 DevKit v1 (30 pins long, 11 pins width): The DOIT Esp32 DevKit v1 is one of the development board created by DOIT to evaluate the ESP-WROOM-32 module. It is based on the ESP32 microcontroller that boasts Wifi, Bluetooth, Ethernet and Low Power support all in a single chip. (vanepp) made breadboard work, adjusted pin numbering and labels and reduced size of schematic and cleaned up pcb. This chip is 30pins long (2 x15) and 11 pins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
